// Logisim project André_Kaled_Duarte_Coutinho_Andrade.circ as structural Verilog: 25 circuits, main circuit main
module main (
);

  wire DATA_ADDRESS, I_O_clk_e, I_O_clk_s, INPUT_OUTPUT, monitor_1_enable, monitor_1_io_clk_s, or_1_out,
       paralela_1_enable, paralela_1_io_clk_s, portio_1_p3, registrador_flags_1_a_lager,
       registrador_flags_1_c_out, registrador_flags_1_equals, registrador_flags_1_zero, teclado_1_clock,
       teclado_1_regis, uc_1_acc_e, uc_1_acc_s, uc_1_bus_1_e, uc_1_flags_s, uc_1_iar_e, uc_1_iar_s,
       uc_1_init, uc_1_ir_s, uc_1_mar_s, uc_1_r0_e, uc_1_r0_s, uc_1_r1_e, uc_1_r1_s, uc_1_r2_e, uc_1_r2_s,
       uc_1_r3_e, uc_1_r3_s, uc_1_ram_e, uc_1_ram_s, uc_1_tmp_s, ula_1_a_lager, ula_1_c_out, ula_1_equals,
       ula_1_zero;
  wire [2:0] uc_1_to_ula;
  wire [6:0] keyboard_1_data, monitor_1_out_5;
  wire [7:0] bus_1_1_out_3, controlled_buffer_1_out, controlled_buffer_7_out, IAR_q, IR_q, R0_q, R1_q, R2_q,
       R3_q, register_1_q, register_2_q, TMP_q, ula_1_saida;

  ULA ula_1 (
    .A(controlled_buffer_1_out), .B(bus_1_1_out_3), .saida(ula_1_saida), .b_1(uc_1_bus_1_e),
    .c_in(registrador_flags_1_c_out), .op(uc_1_to_ula), .c_out(ula_1_c_out), .zero(ula_1_zero),
    .a_lager(ula_1_a_lager), .equals(ula_1_equals));
  Register TMP (.D(controlled_buffer_1_out), .Q(TMP_q), .clk(uc_1_tmp_s));  // open: en, clr
  bus_1 bus_1_1 (.in_1(TMP_q), .out_3(bus_1_1_out_3), .in_2(uc_1_bus_1_e));
  Register register_1 (.D(ula_1_saida), .Q(register_1_q), .clk(uc_1_acc_s));  // open: en, clr
  assign controlled_buffer_1_out = uc_1_acc_e ? register_1_q : 8'bz;  // Controlled_Buffer controlled_buffer_1
  Keyboard keyboard_1 (.clk(teclado_1_clock), .re(teclado_1_regis), .data(keyboard_1_data));  // open: clr, avail
  teclado teclado_1 (
    .I_O_clk_e(I_O_clk_e), .I_O_clk_s(I_O_clk_s), .DATA_ADDRESS(DATA_ADDRESS), .INPUT_OUTPUT(INPUT_OUTPUT),
    .in_1(controlled_buffer_1_out), .out_7(controlled_buffer_1_out), .dado_teclado(keyboard_1_data),
    .clock(teclado_1_clock), .regis(teclado_1_regis));
  registrador_flags registrador_flags_1 (
    .c_out_storage(ula_1_c_out), .zero_storage(ula_1_zero), .a_lager_storage(ula_1_a_lager),
    .equals_storage(ula_1_equals), .set(uc_1_flags_s), .c_out(registrador_flags_1_c_out),
    .a_lager(registrador_flags_1_a_lager), .equals(registrador_flags_1_equals),
    .zero(registrador_flags_1_zero));
  assign controlled_buffer_1_out = uc_1_r0_e ? R0_q : 8'bz;  // Controlled_Buffer controlled_buffer_2
  Register R0 (.D(controlled_buffer_1_out), .Q(R0_q), .clk(uc_1_r0_s));  // open: en, clr
  // Probe on registrador_flags_1_c_out
  // Probe on registrador_flags_1_a_lager
  assign controlled_buffer_1_out = uc_1_r1_e ? R1_q : 8'bz;  // Controlled_Buffer controlled_buffer_3
  Register R1 (.D(controlled_buffer_1_out), .Q(R1_q), .clk(uc_1_r1_s));  // open: en, clr
  // Probe on registrador_flags_1_equals
  // Probe on registrador_flags_1_zero
  Register IAR (.D(controlled_buffer_1_out), .Q(IAR_q), .clk(uc_1_iar_s));  // open: en, clr
  assign controlled_buffer_1_out = uc_1_iar_e ? IAR_q : 8'bz;  // Controlled_Buffer controlled_buffer_4
  monitor monitor_1 (
    .I_O_clk_s(I_O_clk_s), .DATA_ADDRESS(DATA_ADDRESS), .INPUT_OUTPUT(INPUT_OUTPUT),
    .in_1(controlled_buffer_1_out), .out_5(monitor_1_out_5), .IO_clk_s(monitor_1_io_clk_s),
    .enable(monitor_1_enable));
  assign controlled_buffer_1_out = uc_1_r2_e ? R2_q : 8'bz;  // Controlled_Buffer controlled_buffer_5
  Register R2 (.D(controlled_buffer_1_out), .Q(R2_q), .clk(uc_1_r2_s));  // open: en, clr
  Register IR (.D(controlled_buffer_1_out), .Q(IR_q), .clk(uc_1_ir_s));  // open: en, clr
  TTY tty_1 (.data(monitor_1_out_5), .clk(monitor_1_io_clk_s), .we(monitor_1_enable));  // open: clr
  assign controlled_buffer_1_out = uc_1_r3_e ? R3_q : 8'bz;  // Controlled_Buffer controlled_buffer_6
  Register R3 (.D(controlled_buffer_1_out), .Q(R3_q), .clk(uc_1_r3_s));  // open: en, clr
  UC uc_1 (
    .carry_out(registrador_flags_1_c_out), .a_larger(registrador_flags_1_a_lager),
    .equal(registrador_flags_1_equals), .zero(registrador_flags_1_zero), .IR(IR_q),
    .Data_Address(DATA_ADDRESS), .Input_Output(INPUT_OUTPUT), .R0_e(uc_1_r0_e), .R1_e(uc_1_r1_e),
    .R2_e(uc_1_r2_e), .R3_e(uc_1_r3_e), .MAR_s(uc_1_mar_s), .IAR_s(uc_1_iar_s), .ACC_s(uc_1_acc_s),
    .RAM_s(uc_1_ram_s), .TMP_s(uc_1_tmp_s), .FLAGS_s(uc_1_flags_s), .IO_clk_s(I_O_clk_s), .R0_s(uc_1_r0_s),
    .R1_s(uc_1_r1_s), .R2_s(uc_1_r2_s), .R3_s(uc_1_r3_s), .IR_s(uc_1_ir_s), .to_ULA(uc_1_to_ula),
    .bus_1_e(uc_1_bus_1_e), .IAR_e(uc_1_iar_e), .RAM_e(uc_1_ram_e), .ACC_e(uc_1_acc_e), .IO_clk_e(I_O_clk_e),
    .init(uc_1_init));
  LED led_1 (.in(uc_1_init));
  RAM #(.databus("bidir")) ram_1 (.addr(register_2_q), .we(uc_1_ram_s), .oe(uc_1_ram_e), .clk(or_1_out));  // open: data
  Register register_2 (.D(controlled_buffer_1_out), .Q(register_2_q), .clk(uc_1_mar_s));  // open: en, clr
  or or_1 (or_1_out, uc_1_ram_s, uc_1_ram_e);
  paralela paralela_1 (
    .I_O_clk_s(I_O_clk_s), .DATA_ADDRESS(DATA_ADDRESS), .INPUT_OUTPUT(INPUT_OUTPUT),
    .in_1(controlled_buffer_1_out), .IO_clk_s(paralela_1_io_clk_s), .enable(paralela_1_enable));
  // Probe on controlled_buffer_1_out
  assign controlled_buffer_7_out = paralela_1_io_clk_s ? controlled_buffer_1_out : 8'bz;  // Controlled_Buffer controlled_buffer_7
  // PortIO portio_1: pin names not known; wires that end beside it: paralela_1_enable, controlled_buffer_7_out, portio_1_p3, portio_1_p3

  // Notes on the sheet:
  //   22450837
  //   André Kaled Duarte Coutinho Andrade
  //   01 ff 71 77
  //   7c 7a 7b 7d 40 04
endmodule

module somador_1bit (
  input  c_in,
  input  A,
  input  B,
  output output_soma,
  output c_out
);

  wire and_1_out, and_2_out, and_3_out, xor_1_out;

  xor xor_1 (xor_1_out, A, B);
  and and_1 (and_1_out, A, c_in);
  and and_2 (and_2_out, A, B);
  and and_3 (and_3_out, c_in, B);
  xor xor_2 (output_soma, xor_1_out, c_in);
  or or_1 (c_out, and_1_out, and_2_out, and_3_out);
endmodule

module somador_8bits (
  input  [7:0] A,
  input  c_in,
  input  [7:0] B,
  output [7:0] output_soma,
  output c_out
);

  wire input_A_a0, input_A_a1, input_A_a2, input_A_a3, input_A_a4, input_A_a5, input_A_a6, input_A_a7,
       input_B_a0, input_B_a1, input_B_a2, input_B_a3, input_B_a4, input_B_a5, input_B_a6, input_B_a7,
       soma_bit_mais_significativo_output_soma, soma_bit_menos_significativo_c_out,
       soma_bit_menos_significativo_output_soma, somador_1bit_1_c_out, somador_1bit_1_output_soma,
       somador_1bit_2_c_out, somador_1bit_2_output_soma, somador_1bit_3_c_out, somador_1bit_3_output_soma,
       somador_1bit_4_c_out, somador_1bit_4_output_soma, somador_1bit_5_c_out, somador_1bit_5_output_soma,
       somador_1bit_6_c_out, somador_1bit_6_output_soma;

  distribuidor_8bits input_A (
    .A_8bits(A), .A0(input_A_a0), .A1(input_A_a1), .A2(input_A_a2), .A3(input_A_a3), .A4(input_A_a4),
    .A5(input_A_a5), .A6(input_A_a6), .A7(input_A_a7));
  distribuidor_8bits input_B (
    .A_8bits(B), .A0(input_B_a0), .A1(input_B_a1), .A2(input_B_a2), .A3(input_B_a3), .A4(input_B_a4),
    .A5(input_B_a5), .A6(input_B_a6), .A7(input_B_a7));
  somador_1bit soma_bit_menos_significativo (
    .c_in(c_in), .A(input_A_a0), .B(input_B_a0), .output_soma(soma_bit_menos_significativo_output_soma),
    .c_out(soma_bit_menos_significativo_c_out));
  somador_1bit somador_1bit_1 (
    .c_in(soma_bit_menos_significativo_c_out), .A(input_A_a1), .B(input_B_a1),
    .output_soma(somador_1bit_1_output_soma), .c_out(somador_1bit_1_c_out));
  somador_1bit somador_1bit_2 (
    .c_in(somador_1bit_1_c_out), .A(input_A_a2), .B(input_B_a2), .output_soma(somador_1bit_2_output_soma),
    .c_out(somador_1bit_2_c_out));
  somador_1bit somador_1bit_3 (
    .c_in(somador_1bit_2_c_out), .A(input_A_a3), .B(input_B_a3), .output_soma(somador_1bit_3_output_soma),
    .c_out(somador_1bit_3_c_out));
  somador_1bit somador_1bit_4 (
    .c_in(somador_1bit_3_c_out), .A(input_A_a4), .B(input_B_a4), .output_soma(somador_1bit_4_output_soma),
    .c_out(somador_1bit_4_c_out));
  somador_1bit somador_1bit_5 (
    .c_in(somador_1bit_4_c_out), .A(input_A_a5), .B(input_B_a5), .output_soma(somador_1bit_5_output_soma),
    .c_out(somador_1bit_5_c_out));
  somador_1bit somador_1bit_6 (
    .c_in(somador_1bit_5_c_out), .A(input_A_a6), .B(input_B_a6), .output_soma(somador_1bit_6_output_soma),
    .c_out(somador_1bit_6_c_out));
  somador_1bit soma_bit_mais_significativo (
    .c_in(somador_1bit_6_c_out), .A(input_A_a7), .B(input_B_a7),
    .output_soma(soma_bit_mais_significativo_output_soma), .c_out(c_out));
  simplifica_bits output_C (
    .A0(soma_bit_menos_significativo_output_soma), .A1(somador_1bit_1_output_soma),
    .A2(somador_1bit_2_output_soma), .A3(somador_1bit_3_output_soma), .A4(somador_1bit_4_output_soma),
    .A5(somador_1bit_5_output_soma), .A6(somador_1bit_6_output_soma),
    .A7(soma_bit_mais_significativo_output_soma), .A_8bits(output_soma));

  // Notes on the sheet:
  //   C0
  //   C1
  //   C2
  //   C3
  //   C4
  //   C5
  //   C6
  //   C7
endmodule

module simplifica_bits (
  input  A0,
  input  A1,
  input  A2,
  input  A3,
  input  A4,
  input  A5,
  input  A6,
  input  A7,
  output [7:0] A_8bits
);


  assign A_8bits = {A7, A6, A5, A4, A3, A2, A1, A0};
endmodule

module distribuidor_8bits (
  input  [7:0] A_8bits,
  output A0,
  output A1,
  output A2,
  output A3,
  output A4,
  output A5,
  output A6,
  output A7
);


  assign A0 = A_8bits[0];
  assign A1 = A_8bits[1];
  assign A2 = A_8bits[2];
  assign A3 = A_8bits[3];
  assign A4 = A_8bits[4];
  assign A5 = A_8bits[5];
  assign A6 = A_8bits[6];
  assign A7 = A_8bits[7];
endmodule

// R
module registrador_1bit (
  input  input_1bit,
  input  set,
  output bit_armazenado
);

  wire nand_1_out, nand_2_out, nand_4_out;

  nand nand_1 (nand_1_out, input_1bit, set);
  nand nand_2 (nand_2_out, nand_1_out, set);
  nand nand_3 (bit_armazenado, nand_1_out, nand_4_out);
  nand nand_4 (nand_4_out, bit_armazenado, nand_2_out);
endmodule

module registrador_8bits (
  input  [7:0] input_8bits,
  input  set,
  input  enable_in,
  output [7:0] dados
);

  wire distribuidor_8bits_1_a0, distribuidor_8bits_1_a1, distribuidor_8bits_1_a2, distribuidor_8bits_1_a3,
       distribuidor_8bits_1_a4, distribuidor_8bits_1_a5, distribuidor_8bits_1_a6, distribuidor_8bits_1_a7,
       enable_1_output_dado, enable_2_output_dado, enable_3_output_dado, enable_4_output_dado,
       enable_5_output_dado, enable_6_output_dado, enable_7_output_dado, enable_8_output_dado,
       registrador_1bit_1_bit_armazenado, registrador_1bit_2_bit_armazenado,
       registrador_1bit_3_bit_armazenado, registrador_1bit_4_bit_armazenado,
       registrador_1bit_5_bit_armazenado, registrador_1bit_6_bit_armazenado,
       registrador_1bit_7_bit_armazenado, registrador_1bit_8_bit_armazenado;

  distribuidor_8bits distribuidor_8bits_1 (
    .A_8bits(input_8bits), .A0(distribuidor_8bits_1_a0), .A1(distribuidor_8bits_1_a1),
    .A2(distribuidor_8bits_1_a2), .A3(distribuidor_8bits_1_a3), .A4(distribuidor_8bits_1_a4),
    .A5(distribuidor_8bits_1_a5), .A6(distribuidor_8bits_1_a6), .A7(distribuidor_8bits_1_a7));
  registrador_1bit registrador_1bit_1 (
    .input_1bit(distribuidor_8bits_1_a0), .set(set), .bit_armazenado(registrador_1bit_1_bit_armazenado));
  registrador_1bit registrador_1bit_2 (
    .input_1bit(distribuidor_8bits_1_a1), .set(set), .bit_armazenado(registrador_1bit_2_bit_armazenado));
  registrador_1bit registrador_1bit_3 (
    .input_1bit(distribuidor_8bits_1_a2), .set(set), .bit_armazenado(registrador_1bit_3_bit_armazenado));
  registrador_1bit registrador_1bit_4 (
    .input_1bit(distribuidor_8bits_1_a3), .set(set), .bit_armazenado(registrador_1bit_4_bit_armazenado));
  registrador_1bit registrador_1bit_5 (
    .input_1bit(distribuidor_8bits_1_a4), .set(set), .bit_armazenado(registrador_1bit_5_bit_armazenado));
  registrador_1bit registrador_1bit_6 (
    .input_1bit(distribuidor_8bits_1_a5), .set(set), .bit_armazenado(registrador_1bit_6_bit_armazenado));
  registrador_1bit registrador_1bit_7 (
    .input_1bit(distribuidor_8bits_1_a6), .set(set), .bit_armazenado(registrador_1bit_7_bit_armazenado));
  registrador_1bit registrador_1bit_8 (
    .input_1bit(distribuidor_8bits_1_a7), .set(set), .bit_armazenado(registrador_1bit_8_bit_armazenado));
  enable enable_1 (
    .dado(registrador_1bit_1_bit_armazenado), .input_enable(enable_in), .output_dado(enable_1_output_dado));
  enable enable_2 (
    .dado(registrador_1bit_2_bit_armazenado), .input_enable(enable_in), .output_dado(enable_2_output_dado));
  enable enable_3 (
    .dado(registrador_1bit_3_bit_armazenado), .input_enable(enable_in), .output_dado(enable_3_output_dado));
  enable enable_4 (
    .dado(registrador_1bit_4_bit_armazenado), .input_enable(enable_in), .output_dado(enable_4_output_dado));
  enable enable_5 (
    .dado(registrador_1bit_5_bit_armazenado), .input_enable(enable_in), .output_dado(enable_5_output_dado));
  enable enable_6 (
    .dado(registrador_1bit_6_bit_armazenado), .input_enable(enable_in), .output_dado(enable_6_output_dado));
  enable enable_7 (
    .dado(registrador_1bit_7_bit_armazenado), .input_enable(enable_in), .output_dado(enable_7_output_dado));
  enable enable_8 (
    .dado(registrador_1bit_8_bit_armazenado), .input_enable(enable_in), .output_dado(enable_8_output_dado));
  simplifica_bits simplifica_bits_1 (
    .A0(enable_1_output_dado), .A1(enable_2_output_dado), .A2(enable_3_output_dado),
    .A3(enable_4_output_dado), .A4(enable_5_output_dado), .A5(enable_6_output_dado),
    .A6(enable_7_output_dado), .A7(enable_8_output_dado), .A_8bits(dados));
endmodule

// e
module enable (
  input  dado,
  input  input_enable,
  output output_dado
);

  and and_1 (output_dado, dado, input_enable);
endmodule

module shift_left (
  input  c_in,
  input  [7:0] input_shift,
  output [7:0] SHL,
  output c_out
);


  assign c_out = input_shift[7];
  assign SHL = {input_shift[6:0], c_in};
endmodule

module shift_rigth (
  input  c_in,
  input  [7:0] input_shift,
  output [7:0] SHR,
  output c_out
);


  assign c_out = input_shift[0];
  assign SHR = {c_in, input_shift[7:1]};
endmodule

module ULA (
  input  b_1,
  input  c_in,
  input  [2:0] op,
  input  [7:0] A,
  input  [7:0] B,
  output c_out,
  output [7:0] saida,
  output zero,
  output a_lager,
  output equals
);

  wire adder_1_cout, and_1_out, comparator_1_lt, SHIFT_L_c_out, SHIFT_R_c_out;
  wire [7:0] A_AND_B_a_and_b, A_OR_B_a_or_b, A_XOR_B_a_xor_b, adder_1_out, NOT_A_not_a, SHIFT_L_shl,
       SHIFT_R_shr;

  and and_1 (and_1_out, ~b_1, c_in);  // AND_Gate
  Adder adder_1 (.a(B), .b(A), .out(adder_1_out), .cin(and_1_out), .cout(adder_1_cout));
  shift_rigth SHIFT_R (.input_shift(A), .c_in(and_1_out), .c_out(SHIFT_R_c_out), .SHR(SHIFT_R_shr));
  shift_left SHIFT_L (.input_shift(A), .c_in(and_1_out), .c_out(SHIFT_L_c_out), .SHL(SHIFT_L_shl));
  NOTer NOT_A (.A(A), .NOT_A(NOT_A_not_a));
  ANDer A_AND_B (.A(A), .B(B), .A_AND_B(A_AND_B_a_and_b));
  ORer A_OR_B (.A(A), .B(B), .A_OR_B(A_OR_B_a_or_b));
  XORer A_XOR_B (.A(A), .B(B), .A_XOR_B(A_XOR_B_a_xor_b));
  Comparator comparator_1 (.a(A), .b(B), .gt(a_lager), .eq(equals), .lt(comparator_1_lt));
  Multiplexer #(.select(3), .width(8)) multiplexer_1 (
    .in0(adder_1_out), .in1(SHIFT_R_shr), .in2(SHIFT_L_shl), .in3(NOT_A_not_a), .in4(A_AND_B_a_and_b),
    .in5(A_OR_B_a_or_b), .in6(A_XOR_B_a_xor_b), .in7(A), .out(saida), .sel(op));
  Multiplexer #(.select(3)) multiplexer_2 (
    .in0(adder_1_cout), .in1(SHIFT_R_c_out), .in2(SHIFT_L_c_out), .in3(1'b0), .in4(1'b0), .in5(1'b0),
    .in6(1'b0), .in7(1'b0), .out(c_out), .sel(op));
  IS_ZERO is_zero_1 (.A(saida), .output_zero(zero));
endmodule

module NOTer (
  input  [7:0] A,
  output [7:0] NOT_A
);

  assign NOT_A = ~A;  // NOT_Gate not_1, 8 bits wide
endmodule

module ANDer (
  input  [7:0] A,
  input  [7:0] B,
  output [7:0] A_AND_B
);

  assign A_AND_B = A & B;  // AND_Gate and_1, 8 bits wide
endmodule

module ORer (
  input  [7:0] A,
  input  [7:0] B,
  output [7:0] A_OR_B
);

  assign A_OR_B = A | B;  // OR_Gate or_1, 8 bits wide
endmodule

module XORer (
  input  [7:0] A,
  input  [7:0] B,
  output [7:0] A_XOR_B
);

  assign A_XOR_B = A ^ B;  // XOR_Gate xor_1, 8 bits wide
endmodule

module IS_ZERO (
  input  [7:0] A,
  output output_zero
);

  wire distribuidor_8bits_1_a0, distribuidor_8bits_1_a1, distribuidor_8bits_1_a2, distribuidor_8bits_1_a3,
       distribuidor_8bits_1_a4, distribuidor_8bits_1_a5, distribuidor_8bits_1_a6, distribuidor_8bits_1_a7,
       or_1_out;

  distribuidor_8bits distribuidor_8bits_1 (
    .A_8bits(A), .A0(distribuidor_8bits_1_a0), .A1(distribuidor_8bits_1_a1), .A2(distribuidor_8bits_1_a2),
    .A3(distribuidor_8bits_1_a3), .A4(distribuidor_8bits_1_a4), .A5(distribuidor_8bits_1_a5),
    .A6(distribuidor_8bits_1_a6), .A7(distribuidor_8bits_1_a7));
  or or_1 (or_1_out, distribuidor_8bits_1_a0, distribuidor_8bits_1_a1, distribuidor_8bits_1_a2, distribuidor_8bits_1_a3, distribuidor_8bits_1_a4, distribuidor_8bits_1_a5, distribuidor_8bits_1_a6, distribuidor_8bits_1_a7);
  not not_1 (output_zero, or_1_out);
endmodule

module comparador_bit (
  input  anterior_iguais,
  input  A_era_maior,
  input  A,
  input  B,
  output diferentes,
  output iguais,
  output A_maior
);

  wire and_2_out, not_1_out;

  xor xor_1 (diferentes, A, B);
  not not_1 (not_1_out, diferentes);
  and and_1 (iguais, not_1_out, anterior_iguais);
  and and_2 (and_2_out, anterior_iguais, A, diferentes);
  or or_1 (A_maior, and_2_out, A_era_maior);
endmodule

module comparador_geral (
  input  anterior_igual,
  input  a_maior_input,
  input  [7:0] A,
  input  [7:0] B,
  output [7:0] diferenca,
  output equal,
  output maior
);

  wire comparador_bit_1_a_maior, comparador_bit_1_diferentes, comparador_bit_1_iguais,
       comparador_bit_2_a_maior, comparador_bit_2_diferentes, comparador_bit_2_iguais,
       comparador_bit_3_a_maior, comparador_bit_3_diferentes, comparador_bit_3_iguais,
       comparador_bit_4_a_maior, comparador_bit_4_diferentes, comparador_bit_4_iguais,
       comparador_bit_5_a_maior, comparador_bit_5_diferentes, comparador_bit_5_iguais,
       comparador_bit_6_a_maior, comparador_bit_6_diferentes, comparador_bit_6_iguais,
       comparador_bit_7_a_maior, comparador_bit_7_diferentes, comparador_bit_7_iguais,
       comparador_bit_8_diferentes, distribuidor_8bits_1_a0, distribuidor_8bits_1_a1,
       distribuidor_8bits_1_a2, distribuidor_8bits_1_a3, distribuidor_8bits_1_a4, distribuidor_8bits_1_a5,
       distribuidor_8bits_1_a6, distribuidor_8bits_1_a7, distribuidor_8bits_2_a0, distribuidor_8bits_2_a1,
       distribuidor_8bits_2_a2, distribuidor_8bits_2_a3, distribuidor_8bits_2_a4, distribuidor_8bits_2_a5,
       distribuidor_8bits_2_a6, distribuidor_8bits_2_a7;

  distribuidor_8bits distribuidor_8bits_1 (
    .A_8bits(A), .A0(distribuidor_8bits_1_a0), .A1(distribuidor_8bits_1_a1), .A2(distribuidor_8bits_1_a2),
    .A3(distribuidor_8bits_1_a3), .A4(distribuidor_8bits_1_a4), .A5(distribuidor_8bits_1_a5),
    .A6(distribuidor_8bits_1_a6), .A7(distribuidor_8bits_1_a7));
  distribuidor_8bits distribuidor_8bits_2 (
    .A0(distribuidor_8bits_2_a0), .A1(distribuidor_8bits_2_a1), .A2(distribuidor_8bits_2_a2),
    .A3(distribuidor_8bits_2_a3), .A4(distribuidor_8bits_2_a4), .A5(distribuidor_8bits_2_a5),
    .A6(distribuidor_8bits_2_a6), .A7(distribuidor_8bits_2_a7));  // open: A_8bits
  comparador_bit comparador_bit_1 (
    .A(distribuidor_8bits_1_a7), .B(distribuidor_8bits_2_a7), .anterior_iguais(anterior_igual),
    .A_era_maior(a_maior_input), .iguais(comparador_bit_1_iguais), .A_maior(comparador_bit_1_a_maior),
    .diferentes(comparador_bit_1_diferentes));
  comparador_bit comparador_bit_2 (
    .A(distribuidor_8bits_1_a6), .B(distribuidor_8bits_2_a6), .anterior_iguais(comparador_bit_1_iguais),
    .A_era_maior(comparador_bit_1_a_maior), .iguais(comparador_bit_2_iguais),
    .A_maior(comparador_bit_2_a_maior), .diferentes(comparador_bit_2_diferentes));
  comparador_bit comparador_bit_3 (
    .A(distribuidor_8bits_1_a5), .B(distribuidor_8bits_2_a5), .anterior_iguais(comparador_bit_2_iguais),
    .A_era_maior(comparador_bit_2_a_maior), .iguais(comparador_bit_3_iguais),
    .A_maior(comparador_bit_3_a_maior), .diferentes(comparador_bit_3_diferentes));
  comparador_bit comparador_bit_4 (
    .A(distribuidor_8bits_1_a4), .B(distribuidor_8bits_2_a4), .anterior_iguais(comparador_bit_3_iguais),
    .A_era_maior(comparador_bit_3_a_maior), .iguais(comparador_bit_4_iguais),
    .A_maior(comparador_bit_4_a_maior), .diferentes(comparador_bit_4_diferentes));
  comparador_bit comparador_bit_5 (
    .A(distribuidor_8bits_1_a3), .B(distribuidor_8bits_2_a3), .anterior_iguais(comparador_bit_4_iguais),
    .A_era_maior(comparador_bit_4_a_maior), .iguais(comparador_bit_5_iguais),
    .A_maior(comparador_bit_5_a_maior), .diferentes(comparador_bit_5_diferentes));
  comparador_bit comparador_bit_6 (
    .A(distribuidor_8bits_1_a2), .B(distribuidor_8bits_2_a2), .anterior_iguais(comparador_bit_5_iguais),
    .A_era_maior(comparador_bit_5_a_maior), .iguais(comparador_bit_6_iguais),
    .A_maior(comparador_bit_6_a_maior), .diferentes(comparador_bit_6_diferentes));
  comparador_bit comparador_bit_7 (
    .A(distribuidor_8bits_1_a1), .B(distribuidor_8bits_2_a1), .anterior_iguais(comparador_bit_6_iguais),
    .A_era_maior(comparador_bit_6_a_maior), .iguais(comparador_bit_7_iguais),
    .A_maior(comparador_bit_7_a_maior), .diferentes(comparador_bit_7_diferentes));
  comparador_bit comparador_bit_8 (
    .A(distribuidor_8bits_1_a0), .B(distribuidor_8bits_2_a0), .anterior_iguais(comparador_bit_7_iguais),
    .A_era_maior(comparador_bit_7_a_maior), .iguais(equal), .A_maior(maior),
    .diferentes(comparador_bit_8_diferentes));
  simplifica_bits simplifica_bits_1 (
    .A0(comparador_bit_1_diferentes), .A1(comparador_bit_2_diferentes), .A2(comparador_bit_3_diferentes),
    .A3(comparador_bit_4_diferentes), .A4(comparador_bit_5_diferentes), .A5(comparador_bit_6_diferentes),
    .A6(comparador_bit_7_diferentes), .A7(comparador_bit_8_diferentes), .A_8bits(diferenca));
endmodule

module bus_1 (
  input  [7:0] in_1,
  input  in_2,
  output [7:0] out_3
);

  Multiplexer #(.enable("true"), .width(8)) multiplexer_1 (
    .in0(in_1), .in1(8'h1), .out(out_3), .sel(in_2));  // open: en
endmodule

module meu_clock (
  output set,
  output enable
);

  wire clok_out, not_1_out, t_ff_1_q;

  Clock clok (.out(clok_out));
  not not_1 (not_1_out, clok_out);
  T_Flip_Flop t_ff_1 (.clk(clok_out), .T(1'b1), .Q(t_ff_1_q));  // open: Qn, preset, reset
  and and_1 (set, not_1_out, t_ff_1_q);
  or or_1 (enable, t_ff_1_q, clok_out);
endmodule

module UC (
  input  carry_out,
  input  a_larger,
  input  equal,
  input  zero,
  input  [7:0] IR,
  output init,
  output IR_s,
  output bus_1_e,
  output IAR_e,
  output MAR_s,
  output RAM_e,
  output IAR_s,
  output ACC_e,
  output ACC_s,
  output IO_clk_e,
  output RAM_s,
  output TMP_s,
  output FLAGS_s,
  output IO_clk_s,
  output R0_e,
  output R1_e,
  output R2_e,
  output R3_e,
  output R0_s,
  output R1_s,
  output R2_s,
  output R3_s,
  output Data_Address,
  output Input_Output,
  output [2:0] to_ULA
);

  wire A_out, and_5_out, and_6_out, and_7_out, and_8_out, and_9_out, and_10_out, and_11_out, and_12_out,
       and_16_out, and_17_out, and_18_out, and_19_out, and_20_out, and_21_out, and_22_out, and_23_out,
       and_24_out, and_25_out, and_26_out, and_27_out, and_28_out, and_29_out, and_30_out, and_31_out,
       and_32_out, and_33_out, and_34_out, and_35_out, and_36_out, and_37_out, and_38_out, and_39_out,
       and_40_out, and_41_out, and_42_out, and_43_out, C_out, decoder_1_out0, decoder_1_out1, decoder_1_out2,
       decoder_1_out3, decoder_2_out0, decoder_2_out1, decoder_2_out2, decoder_2_out3, decoder_3_out0,
       decoder_3_out1, decoder_3_out2, decoder_3_out3, decoder_3_out4, decoder_3_out5, decoder_3_out6,
       decoder_3_out7, decoder_4_out1, decoder_4_out2, decoder_4_out3, decoder_4_out4, decoder_4_out5,
       decoder_4_out6, decoder_4_out7, decoder_5_out0, decoder_5_out1, decoder_5_out2, decoder_5_out3, E_out,
       meu_clock_1_enable, meu_clock_1_set, not_1_out, not_2_out, not_3_out, or_6_out, or_7_out, or_8_out,
       or_9_out, or_10_out, or_11_out, or_12_out, or_13_out, or_14_out, or_15_out, or_16_out, Z_out;
  wire [2:0] counter_1_q;

  or or_1 (R0_e, and_5_out, and_9_out);
  or or_2 (R1_e, and_6_out, and_10_out);
  or or_3 (R2_e, and_7_out, and_11_out);
  or or_4 (R3_e, and_8_out, and_12_out);
  and and_1 (IAR_e, meu_clock_1_enable, or_6_out);
  and and_2 (RAM_e, meu_clock_1_enable, or_7_out);
  and and_3 (ACC_e, meu_clock_1_enable, or_8_out);
  and and_4 (IO_clk_e, meu_clock_1_enable, and_34_out);
  and and_5 (and_5_out, or_9_out, meu_clock_1_enable, decoder_1_out0);
  and and_6 (and_6_out, or_9_out, meu_clock_1_enable, decoder_1_out1);
  and and_7 (and_7_out, or_9_out, meu_clock_1_enable, decoder_1_out2);
  and and_8 (and_8_out, or_9_out, meu_clock_1_enable, decoder_1_out3);
  and and_9 (and_9_out, or_10_out, meu_clock_1_enable, decoder_2_out0);
  and and_10 (and_10_out, or_10_out, meu_clock_1_enable, decoder_2_out1);
  and and_11 (and_11_out, or_10_out, meu_clock_1_enable, decoder_2_out2);
  and and_12 (and_12_out, or_10_out, meu_clock_1_enable, decoder_2_out3);
  Counter #(.max('h7), .width(3)) counter_1 (
    .D(3'b001), .Q(counter_1_q), .clk(meu_clock_1_enable), .clr(decoder_4_out7));  // open: load, count, carry, up
  meu_clock meu_clock_1 (.set(meu_clock_1_set), .enable(meu_clock_1_enable));
  and and_13 (to_ULA[0], decoder_4_out5, IR[7], IR[4]);
  and and_14 (to_ULA[1], decoder_4_out5, IR[7], IR[5]);
  and and_15 (to_ULA[2], decoder_4_out5, IR[7], IR[6]);
  Decoder #(.enable("false"), .select(2)) decoder_1 (
    .out0(decoder_1_out0), .out1(decoder_1_out1), .out2(decoder_1_out2), .out3(decoder_1_out3), .sel(IR[1:0]));
  Decoder #(.enable("false"), .select(2)) decoder_2 (
    .out0(decoder_2_out0), .out1(decoder_2_out1), .out2(decoder_2_out2), .out3(decoder_2_out3), .sel(IR[3:2]));
  or or_5 (bus_1_e, decoder_4_out1, and_32_out, and_31_out, and_28_out);
  or or_6 (or_6_out, decoder_4_out1, and_28_out, and_30_out, and_31_out);
  or or_7 (or_7_out, decoder_4_out2, and_43_out, and_39_out, and_38_out, and_36_out);
  or or_8 (or_8_out, decoder_4_out3, and_40_out, and_42_out, and_41_out);
  or or_9 (or_9_out, and_25_out, and_37_out, and_29_out, and_33_out);
  or or_10 (or_10_out, and_27_out, and_26_out, and_35_out);
  not not_1 (not_1_out, IR[7]);
  Decoder #(.enable("false"), .select(3)) decoder_3 (
    .out0(decoder_3_out0), .out1(decoder_3_out1), .out2(decoder_3_out2), .out3(decoder_3_out3),
    .out4(decoder_3_out4), .out5(decoder_3_out5), .out6(decoder_3_out6), .out7(decoder_3_out7), .sel(IR[6:4]));
  and C (C_out, IR[3], carry_out);
  and A (A_out, IR[2], a_larger);
  and E (E_out, IR[1], equal);
  and Z (Z_out, IR[0], zero);
  and and_16 (and_16_out, not_1_out, decoder_3_out0);
  and and_17 (and_17_out, not_1_out, decoder_3_out1);
  and and_18 (and_18_out, not_1_out, decoder_3_out2);
  and and_19 (and_19_out, not_1_out, decoder_3_out3);
  and and_20 (and_20_out, not_1_out, decoder_3_out4);
  and and_21 (and_21_out, not_1_out, decoder_3_out5);
  and and_22 (and_22_out, not_1_out, decoder_3_out6);
  and and_23 (and_23_out, not_1_out, decoder_3_out7);
  and and_24 (and_24_out, IR[4], IR[5], IR[6]);
  not not_2 (not_2_out, and_24_out);
  Decoder #(.enable("false"), .select(3)) decoder_4 (
    .out0(init), .out1(decoder_4_out1), .out2(decoder_4_out2), .out3(decoder_4_out3), .out4(decoder_4_out4),
    .out5(decoder_4_out5), .out6(decoder_4_out6), .out7(decoder_4_out7), .sel(counter_1_q));
  and and_25 (and_25_out, decoder_4_out4, IR[7]);
  and and_26 (and_26_out, decoder_4_out4, and_16_out);
  and and_27 (and_27_out, decoder_4_out4, and_17_out);
  and and_28 (and_28_out, decoder_4_out4, and_18_out);
  and and_29 (and_29_out, decoder_4_out4, and_19_out);
  and and_30 (and_30_out, decoder_4_out4, and_20_out);
  and and_31 (and_31_out, decoder_4_out4, and_21_out);
  and and_32 (and_32_out, decoder_4_out4, and_22_out);
  and and_33 (and_33_out, decoder_4_out4, and_23_out, IR[3]);
  not not_3 (not_3_out, IR[3]);
  or or_11 (or_11_out, C_out, A_out, E_out, Z_out);
  and and_34 (and_34_out, decoder_4_out5, and_23_out, not_3_out);
  and and_35 (and_35_out, decoder_4_out5, IR[7]);
  and and_36 (and_36_out, decoder_4_out5, and_16_out);
  and and_37 (and_37_out, decoder_4_out5, and_17_out);
  and and_38 (and_38_out, decoder_4_out5, and_18_out);
  and and_39 (and_39_out, decoder_4_out5, and_20_out);
  and and_40 (and_40_out, decoder_4_out5, and_21_out);
  and and_41 (and_41_out, decoder_4_out6, IR[7], not_2_out);
  and and_42 (and_42_out, decoder_4_out6, and_18_out);
  and and_43 (and_43_out, decoder_4_out6, and_21_out, or_11_out);
  or or_12 (or_12_out, and_36_out, and_41_out, and_38_out, and_34_out);
  Decoder #(.enable("false"), .select(2)) decoder_5 (
    .out0(decoder_5_out0), .out1(decoder_5_out1), .out2(decoder_5_out2), .out3(decoder_5_out3), .sel(IR[1:0]));
  or or_13 (or_13_out, decoder_4_out1, and_28_out, and_31_out, and_26_out, and_27_out, and_30_out);
  or or_14 (or_14_out, decoder_4_out3, and_29_out, and_39_out, and_40_out, and_42_out, and_43_out);
  or or_15 (or_15_out, decoder_4_out1, and_28_out, and_31_out, and_35_out);
  or or_16 (or_16_out, and_32_out, and_35_out);
  and and_44 (MAR_s, meu_clock_1_set, or_13_out);
  and and_45 (IAR_s, meu_clock_1_set, or_14_out);
  and and_46 (ACC_s, meu_clock_1_set, or_15_out);
  and and_47 (RAM_s, meu_clock_1_set, and_37_out);
  and and_48 (TMP_s, meu_clock_1_set, and_25_out);
  and and_49 (FLAGS_s, meu_clock_1_set, or_16_out);
  and and_50 (IO_clk_s, meu_clock_1_set, and_33_out);
  and and_51 (R0_s, meu_clock_1_set, or_12_out, decoder_5_out0);
  and and_52 (R1_s, meu_clock_1_set, or_12_out, decoder_5_out1);
  and and_53 (R2_s, meu_clock_1_set, or_12_out, decoder_5_out2);
  and and_54 (R3_s, meu_clock_1_set, or_12_out, decoder_5_out3);
  and and_55 (IR_s, meu_clock_1_set, decoder_4_out2);

  assign Data_Address = IR[2];
  assign Input_Output = IR[3];

  // Notes on the sheet:
  //   all enables
  //   Reg B
  //   Reg A
  //   Reg B
  //   all sets
endmodule

module registrador_flags (
  input  c_out_storage,
  input  zero_storage,
  input  a_lager_storage,
  input  equals_storage,
  input  set,
  output c_out,
  output a_lager,
  output equals,
  output zero
);

  Register #(.width(1)) register_1 (.D(c_out_storage), .Q(c_out), .clk(set));  // open: en, clr
  Register #(.width(1)) register_2 (.D(zero_storage), .Q(zero), .clk(set));  // open: en, clr
  Register #(.width(1)) register_3 (.D(a_lager_storage), .Q(a_lager), .clk(set));  // open: en, clr
  Register #(.width(1)) register_4 (.D(equals_storage), .Q(equals), .clk(set));  // open: en, clr
endmodule

module teclado (
  input  [7:0] in_1,
  input  I_O_clk_e,
  input  I_O_clk_s,
  input  [6:0] dado_teclado,
  input  DATA_ADDRESS,
  input  INPUT_OUTPUT,
  output [7:0] out_7,
  output clock,
  output regis
);

  wire and_1_out, comparator_1_eq;
  wire [7:0] bit_extender_1_out;

  Comparator comparator_1 (.a(in_1), .b({8{1'b0}}), .eq(comparator_1_eq));  // open: gt, lt
  and and_1 (and_1_out, I_O_clk_s, DATA_ADDRESS, INPUT_OUTPUT);
  T_Flip_Flop t_ff_1 (.clk(I_O_clk_e), .T(1'b1), .Qn(clock));  // open: Q, preset, reset
  Register #(.width(1)) register_1 (.D(comparator_1_eq), .Q(regis), .clk(and_1_out));  // open: en, clr
  // Probe on dado_teclado
  assign bit_extender_1_out = {{1{1'b0}}, dado_teclado};  // Bit_Extender bit_extender_1
  assign out_7 = I_O_clk_e ? bit_extender_1_out : 8'bz;  // Controlled_Buffer controlled_buffer_1
  // Probe on out_7
endmodule

module monitor (
  input  [7:0] in_1,
  input  I_O_clk_s,
  input  DATA_ADDRESS,
  input  INPUT_OUTPUT,
  output [6:0] out_5,
  output IO_clk_s,
  output enable
);

  wire and_1_out, comparator_1_eq;

  Comparator comparator_1 (.a(in_1), .b(8'h1), .eq(comparator_1_eq));  // open: gt, lt
  and and_1 (and_1_out, I_O_clk_s, DATA_ADDRESS, INPUT_OUTPUT);
  Bit_Extender #(.out_width(7)) bit_extender_1 (.in(in_1), .out(out_5));
  Register #(.width(1)) register_1 (.D(comparator_1_eq), .Q(enable), .clk(and_1_out));  // open: en, clr

  assign IO_clk_s = I_O_clk_s;
endmodule

module paralela (
  input  [7:0] in_1,
  input  I_O_clk_s,
  input  DATA_ADDRESS,
  input  INPUT_OUTPUT,
  output IO_clk_s,
  output enable
);

  wire and_1_out, comparator_1_eq;

  Comparator comparator_1 (.a(in_1), .b(8'h2), .eq(comparator_1_eq));  // open: gt, lt
  and and_1 (and_1_out, I_O_clk_s, DATA_ADDRESS, INPUT_OUTPUT);
  Register #(.width(1)) register_1 (.D(comparator_1_eq), .Q(enable), .clk(and_1_out));  // open: en, clr

  assign IO_clk_s = I_O_clk_s;
endmodule
